# Fritzing sketch rpi_weather (saved by Fritzing 0.9.3b)

parts:
  Part1 = BME280 Breakout
  MCU1 = Raspberry Pi Zero

nets:
  N1: Part1.GND, MCU1.pin_14, MCU1.pin_39
  N2: Part1.3.3V, MCU1.pin_1, MCU1.pin_17
  N3: Part1.SDI/SDA, MCU1.pin_3
  N4: Part1.SCK/SCL, MCU1.pin_5
